# Fritzing sketch fritzing-crappy (saved by Fritzing 0.9.3b)
breadboards: 1

parts:
  Part1 = Arduino Board Ethernet
  R1 = Resistor [tolerance=±5% resistance=220 package="0402 [SMD]"]

nets:
  N1: Part1.A0, R1.Pin_0
  N2: Part1.5V, R1.Pin_1
